# Fritzing sketch KnightRider7 (saved by Fritzing 0.7.10b)
breadboards: 2

parts:
  U1 = Arduino Mega
  R1 = Resistor [tolerance=±5% resistance=220 package=THT]
  R2 = Resistor [tolerance=±5% resistance=220 package=THT]
  R3 = Resistor [tolerance=±5% resistance=220 package=THT]
  R4 = Resistor [tolerance=±5% resistance=220 package=THT]
  R5 = Resistor [tolerance=±5% resistance=220 package=THT]
  R6 = Resistor [tolerance=±5% resistance=220 package=THT]
  R7 = Resistor [tolerance=±5% resistance=220 package=THT]
  R8 = Resistor [tolerance=±5% resistance=220 package=THT]
  R9 = Resistor [tolerance=±5% resistance=220 package=THT]
  R10 = Resistor [tolerance=±5% resistance=220 package=THT]
  LED2 = LED - 5mm [color="Red (633nm)" package="5 mm [THT]"]
  LED3 = LED - 5mm [color="Red (633nm)" package="5 mm [THT]"]
  LED4 = LED - 5mm [color="Red (633nm)" package="5 mm [THT]"]
  LED5 = LED - 5mm [color="Red (633nm)" package="5 mm [THT]"]
  LED6 = LED - 5mm [color="Red (633nm)" package="5 mm [THT]"]
  LED7 = LED - 5mm [color="Red (633nm)" package="5 mm [THT]"]
  LED8 = LED - 5mm [color="Red (633nm)" package="5 mm [THT]"]
  LED9 = LED - 5mm [color="Red (633nm)" package="5 mm [THT]"]
  LED10 = LED - 5mm [color="Red (633nm)" package="5 mm [THT]"]
  LED1 = LED - 5mm [color="Red (633nm)" package="5 mm [THT]"]
  R15 = Resistor [tolerance=±5% resistance=220 package=THT]
  R16 = Resistor [tolerance=±5% resistance=220 package=THT]
  R17 = Resistor [tolerance=±5% resistance=220 package=THT]
  R18 = Resistor [tolerance=±5% resistance=220 package=THT]
  R19 = Resistor [tolerance=±5% resistance=220 package=THT]
  R20 = Resistor [tolerance=±5% resistance=220 package=THT]
  LED11 = LED - 5mm [color="Red (633nm)" package="5 mm [THT]"]
  LED16 = LED - 5mm [color="Red (633nm)" package="5 mm [THT]"]
  LED17 = LED - 5mm [color="Red (633nm)" package="5 mm [THT]"]
  LED18 = LED - 5mm [color="Red (633nm)" package="5 mm [THT]"]
  LED19 = LED - 5mm [color="Red (633nm)" package="5 mm [THT]"]
  LED20 = LED - 5mm [color="Red (633nm)" package="5 mm [THT]"]
  Arduino1 = Arduino

nets:
  N1: U1.GND, LED2.cathode, LED3.cathode, LED4.cathode, LED5.cathode, LED6.cathode, LED7.cathode, LED8.cathode, LED9.cathode, LED10.cathode, LED1.cathode
  N2: U1.D11, R1.Pin_0
  N3: U1.D10, R2.Pin_0
  N4: U1.D9, R3.Pin_0
  N5: U1.D8, R4.Pin_0
  N6: U1.D7, R5.Pin_0
  N7: U1.D6, R6.Pin_0
  N8: U1.D5, R7.Pin_0
  N9: U1.D4, R8.Pin_0
  N10: U1.D3, R9.Pin_0
  N11: U1.D2, R10.Pin_0
  N12: R1.Pin_1, LED1.anode
  N13: R2.Pin_1, LED2.anode
  N14: R3.Pin_1, LED3.anode
  N15: R4.Pin_1, LED4.anode
  N16: R5.Pin_1, LED5.anode
  N17: R6.Pin_1, LED6.anode
  N18: R7.Pin_1, LED7.anode
  N19: R8.Pin_1, LED8.anode
  N20: R9.Pin_1, LED9.anode
  N21: R10.Pin_1, LED10.anode
  N22: R15.Pin_0, Arduino1.D3
  N23: R15.Pin_1, LED17.anode
  N24: R16.Pin_0, Arduino1.D5
  N25: R16.Pin_1, LED19.anode
  N26: R17.Pin_1, LED20.anode
  N27: R18.Pin_1, LED11.anode
  N28: R19.Pin_1, LED16.anode
  N29: R20.Pin_0, Arduino1.D6
  N30: R20.Pin_1, LED18.anode
  N31: LED11.cathode, LED16.cathode, LED17.cathode, LED18.cathode, LED19.cathode, LED20.cathode, Arduino1.GND
