# Fritzing sketch super_color (saved by Fritzing 0.7.10b)
breadboards: 1

parts:
  J1 = Basic Force Sensing Resistor (FSR) [package=THT]
  J2 = Basic Force Sensing Resistor (FSR) [package=THT]
  LED1 = RGB LED (com. anode, rbg) [package="5 mm [THT]"]
  LCD1 = LCD screen
  R4 = Trimmer Potentiometer [maximum_resistance=10kΩ package=THT]
  Arduino1 = Arduino
  S1 = Pushbutton [package="[THT]"]
  R5 = Resistor [tolerance=±5% resistance=10k package=THT]
  R6 = Resistor [tolerance=±5% resistance=220 package=THT]
  R7 = Resistor [tolerance=±5% resistance=220 package=THT]
  R8 = Resistor [tolerance=±5% resistance=220 package=THT]

nets:
  VSS: J1.pin_0, J2.pin_0, LCD1.VSS, LCD1.V0, LCD1.R/W, LCD1.DB5, LCD1.LED-, R4.leg1, Arduino1.GND, Arduino1.D9, S1.Pin_3, S1.Pin_4
  N1: J1.pin_1, Arduino1.D2
  N2: J2.pin_1, Arduino1.D4
  N3: LED1.red_cathode, R6.Pin_1
  VDD: LED1.common_anode, LCD1.VDD, LCD1.DB7, LCD1.LED+, R4.leg2, Arduino1.D13, Arduino1.D7, Arduino1.+5V, R5.Pin_1
  N4: LED1.blue_cathode, R7.Pin_1
  N5: LED1.green_cathode, R8.Pin_1
  N6: LCD1.RS, Arduino1.D12
  N7: LCD1.E, Arduino1.D11
  N8: LCD1.DB4, Arduino1.D10
  N9: LCD1.DB6, Arduino1.D8
  N10: R4.wiper, Arduino1.A0
  N11: Arduino1.D6, R7.Pin_0
  N12: Arduino1.D5, R8.Pin_0
  N13: Arduino1.D3, R6.Pin_0
  N14: Arduino1.A1, S1.Pin_1, S1.Pin_2, R5.Pin_0

notes:
  Force resistors may be
  replaced with momentary buttons.
